// Logisim project 6651071022_LAB2_4.circ as structural Verilog: 1 circuit, main circuit main
module main (
  input  A3,
  input  A2,
  input  B3,
  input  B2,
  input  A1,
  input  A0,
  input  B1,
  input  B0,
  output D3,
  output D2,
  output Borrow,
  output D1,
  output D0
);

  wire and_1_out, and_2_out, and_3_out, and_4_out, and_5_out, and_6_out, and_7_out, and_8_out, not_1_out,
       not_2_out, not_4_out, not_5_out, or_1_out, or_2_out, or_3_out, or_4_out, xor_1_out, xor_2_out,
       xor_5_out, xor_6_out;

  not not_1 (not_1_out, B3);
  not not_2 (not_2_out, B1);
  xor xor_1 (xor_1_out, A3, not_1_out);
  and and_1 (and_1_out, A3, not_1_out);
  xor xor_2 (xor_2_out, A1, not_2_out);
  and and_2 (and_2_out, A1, not_2_out);
  xor xor_3 (D1, xor_2_out, or_4_out);
  and and_3 (and_3_out, xor_2_out, or_4_out);
  xor xor_4 (D3, xor_1_out, or_3_out);
  and and_4 (and_4_out, xor_1_out, or_3_out);
  or or_1 (or_1_out, and_2_out, and_3_out);
  or or_2 (or_2_out, and_1_out, and_4_out);
  not not_3 (Borrow, or_2_out);
  not not_4 (not_4_out, B0);
  not not_5 (not_5_out, B2);
  xor xor_5 (xor_5_out, A2, not_5_out);
  and and_5 (and_5_out, A2, not_5_out);
  xor xor_6 (xor_6_out, A0, not_4_out);
  and and_6 (and_6_out, A0, not_4_out);
  xor xor_7 (D2, xor_5_out, or_1_out);
  and and_7 (and_7_out, xor_5_out, or_1_out);
  xor xor_8 (D0, xor_6_out, 1'b1);
  and and_8 (and_8_out, xor_6_out, 1'b1);
  or or_3 (or_3_out, and_5_out, and_7_out);
  or or_4 (or_4_out, and_6_out, and_8_out);

  // Notes on the sheet:
  //   Nguyễn Đức Hiền_6651071022
endmodule
